// Logisim project better_y86_processor.circ as structural Verilog
module PC_Logic (
);

  Register register_1 ();  // open: D, en, Q, clk, clr
  Adder adder_1 ();  // open: a, b, out, cin, cout
  Multiplexer #(.enable("false")) multiplexer_1 ();  // open: in0, in1, out, sel
endmodule

module ALU (
  input  [4:0] operation_select,
  input  [7:0] valA,
  input  [7:0] valB,
  output [7:0] alu_out
);

  wire [7:0] adder_1_out, multiplier_1_out, subtractor_1_out, undriven;

  Adder adder_1 (.a(valA), .b(undriven), .out(adder_1_out));  // open: cin, cout
  Subtractor subtractor_1 (.a(valA), .b(valB), .out(subtractor_1_out));  // open: bin, bout
  Multiplier multiplier_1 (.a(valA), .b(undriven), .out(multiplier_1_out));  // open: cin, cout
  Multiplexer #(.select(5), .width(8), .enable("false")) multiplexer_1 (
    .in0(adder_1_out), .in1(subtractor_1_out), .in2(multiplier_1_out), .out(alu_out), .sel(operation_select));  // open: in3, in4, in5, in6, in7, in8, in9, in10, in11, in12, in13, in14, in15, in16, in17, in18, in19, in20, in21, in22, in23, in24, in25, in26, in27, in28, in29, in30, in31
endmodule
